# Fritzing sketch EMDR (saved by Fritzing 0.9.3b)
circuit board: 7.5cm x 6.1cm

parts:
  ESP32 = Wemos Lolin32lite
  OLED1 = Module display OLED I2C 128x64 SSD1306 [package=THT]  # not connected
  5v_-_3_3v1 = Voltage Regulator [package=to220-adj]
  ALIM = screw terminal, 2 pins
  J8 = screw terminal, 4 pins
  Gnd = screw terminal, 18 pins
  MM5451 = AT89S51
  J7 = screw terminal, 9 pins
  J9 = screw terminal, 9 pins
  R1 = Resistor [tolerance=±5% resistance=220 package=THT]
  LED-B = LED - 5mm [color="Green (560nm)" package="5 mm [THT]"]
  R2 = Resistor [tolerance=±5% resistance=220 package=THT]
  LED-G = LED - 5mm [color="Green (560nm)" package="5 mm [THT]"]
  J10 = screw terminal, 4 pins

nets:
  N1: ESP32.pin_4, J8.pin2
  N2: ESP32.pin_5, J8.pin1
  N3: ESP32.pin_10, MM5451.P1.1_(T2EX)
  N4: ESP32.pin_11, MM5451.P1.0_(T2)
  N5: ESP32.pin_12, MM5451.P0.0_(AD0)
  N6: ESP32.pin_13, 5v_-_3_3v1.ADJ, ALIM.pin1, J8.pin4, Gnd.pin18, MM5451.VCC, LED-B.cathode, LED-G.cathode, J10.pin4
  N7: ESP32.pin_16, J10.pin2
  N8: ESP32.pin_17, J10.pin3
  N9: ESP32.pin_27, R1.Pin_0
  N10: ESP32.pin_28, 5v_-_3_3v1.OUT, J8.pin3, R2.Pin_0, J10.pin1
  N11: 5v_-_3_3v1.IN, ALIM.pin2, MM5451.P2.0_(A8)
  N12: Gnd.pin1, MM5451.P2.1_(A9)
  N13: Gnd.pin2, MM5451.P2.2_(A10)
  N14: Gnd.pin3, MM5451.P2.3_(A11)
  N15: Gnd.pin4, MM5451.P2.4_(A12)
  N16: Gnd.pin5, MM5451.P2.5_(A13)
  N17: Gnd.pin6, MM5451.P2.6_(A14)
  N18: Gnd.pin7, MM5451.P2.7_(A15)
  N19: Gnd.pin8, MM5451.~PSEN
  N20: Gnd.pin9, MM5451.ALE/~PROG
  N21: Gnd.pin10, MM5451.P3.2_(~INT0), MM5451.~EA/VPP, J7.pin1
  N22: Gnd.pin11, MM5451.P3.1_(TXD), MM5451.P0.7_(AD7), J9.pin9
  N23: Gnd.pin12, MM5451.P0.6_(AD6)
  N24: Gnd.pin13, MM5451.P0.5_(AD5)
  N25: Gnd.pin14, MM5451.P0.4_(AD4)
  N26: Gnd.pin15, MM5451.P0.3_(AD3)
  N27: Gnd.pin16, MM5451.P0.2_(AD2)
  N28: Gnd.pin17, MM5451.P0.1_(AD1)
  N29: MM5451.P1.2, J9.pin1
  N30: MM5451.P1.3, J9.pin2
  N31: MM5451.P1.4, J9.pin3
  N32: MM5451.P1.5_(MOSI), J9.pin4
  N33: MM5451.P1.6_(MISO), J9.pin5
  N34: MM5451.P1.7_(SCK), J9.pin6
  N35: MM5451.RESET, J9.pin7
  N36: MM5451.P3.0_(RXD), J9.pin8
  N37: MM5451.P3.3_(~INT1), J7.pin2
  N38: MM5451.P3.4_(T0), J7.pin3
  N39: MM5451.P3.5_(T1), J7.pin4
  N40: MM5451.P3.6_(~WR), J7.pin5
  N41: MM5451.P3.7_(~RD), J7.pin6
  N42: MM5451.XTAL2, J7.pin7
  N43: MM5451.XTAL1, J7.pin8
  N44: MM5451.GND, J7.pin9
  N45: R1.Pin_1, LED-B.anode
  N46: R2.Pin_1, LED-G.anode

notes:
  Gnd
  5v
  sda
  scl
  gnd
  vcc
  3.3v
  bri
  data
  clk
  15
  13

custom parts:
  Wemos Lolin32lite: Wemos Lolinlite32 wifi and blue tooth board based on the ESP-32 cpu, digital I/Os 19, analog inputs 6, clock 240mhz, Flash 4Mbytes, lipo battery charger (500ma connection broken out on breadboard but not pcb), usb.
  Module display OLED I2C 128x64 SSD1306: Ecran OLED I2C SSD163 de 128x64 avec connexion I2C
  AT89S51: AT89S51 DIP40 from Atmel
